// Logisim project 2.circ as structural Verilog: 1 circuit, main circuit main
module main (
  input  in_1,
  input  in_2,
  input  in_3,
  input  in_4,
  input  in_5,
  input  in_6,
  input  in_7,
  input  in_8,
  input  in_9,
  input  in_10,
  input  in_11,
  input  in_12,
  output out_13,
  output out_14
);

  wire and_1_out, and_2_out, multiplexer_1_out, nand_1_out, nor_1_out, not_1_out, not_2_out, not_3_out,
       or_1_out, xnor_1_out, xnor_2_out, xor_1_out;

  xnor xnor_1 (xnor_1_out, in_3, in_4);
  nor nor_1 (nor_1_out, in_3, in_4);
  xor xor_1 (xor_1_out, in_5, in_6);
  and and_1 (and_1_out, in_5, in_6);
  not not_1 (not_1_out, in_5);
  or or_1 (or_1_out, not_1_out, in_6);
  not not_2 (not_2_out, nor_1_out);
  xnor xnor_2 (xnor_2_out, in_5, in_6);
  Multiplexer #(.select(2)) multiplexer_1 (
    .in0(xor_1_out), .in1(xnor_2_out), .in2(and_1_out), .in3(or_1_out), .out(multiplexer_1_out),
    .sel({in_7, in_8}));  // open: en
  not not_3 (not_3_out, in_10);
  and and_2 (and_2_out, in_10, in_9);
  Multiplexer #(.select(2)) multiplexer_2 (
    .in0(in_4), .in1(xnor_1_out), .in2(nor_1_out), .in3(not_2_out), .out(out_13), .sel({in_1, in_2}));  // open: en
  LED led_1 (.in(multiplexer_1_out));
  nand nand_1 (nand_1_out, in_9, not_3_out);
  Multiplexer #(.select(2)) multiplexer_3 (
    .in0(in_10), .in1(not_3_out), .in2(and_2_out), .in3(nand_1_out), .out(out_14), .sel({in_11, in_12}));  // open: en
endmodule
