// Logisim project Circuit1.circ as structural Verilog: 1 circuit, main circuit main
module main (
  input  in_1,
  input  in_2,
  input  in_3,
  input  in_4,
  output out_5
);

  wire and_1_out, and_2_out, and_3_out, and_4_out, not_1_out, not_2_out, not_3_out, not_4_out, not_5_out,
       or_1_out;

  not not_1 (not_1_out, in_1);
  not not_2 (not_2_out, in_2);
  not not_3 (not_3_out, in_1);
  and and_1 (and_1_out, not_1_out, not_2_out, in_4);
  and and_2 (and_2_out, in_1, in_2, in_3);
  and and_3 (and_3_out, not_3_out, in_3, in_4);
  and and_4 (and_4_out, or_1_out, not_4_out, not_5_out);
  not not_4 (not_4_out, in_3);
  not not_5 (not_5_out, in_4);
  or or_1 (or_1_out, in_1, in_2);
  or or_2 (out_5, and_4_out, and_2_out, and_3_out, and_1_out);
endmodule
