// Logisim project circ4.circ as structural Verilog: 1 circuit, main circuit main
// Q1
module main (
);

  wire and_1_out, clock_1_out, Q1_q, Q1_qn, Q2_q, Q3_q, xor_1_out, xor_2_out;

  Clock clock_1 (.out(clock_1_out));
  D_Flip_Flop Q1 (.clk(clock_1_out), .D(Q1_qn), .Q(Q1_q), .Qn(Q1_qn));  // open: preset, en, reset
  and and_1 (and_1_out, Q1_q, Q2_q);
  xor xor_1 (xor_1_out, and_1_out, Q3_q);
  D_Flip_Flop Q3 (.clk(clock_1_out), .D(xor_1_out), .Q(Q3_q));  // open: Qn, preset, en, reset
  xor xor_2 (xor_2_out, Q1_q, Q2_q);
  D_Flip_Flop Q2 (.clk(clock_1_out), .D(xor_2_out), .Q(Q2_q));  // open: Qn, preset, en, reset

  // Notes on the sheet:
  //   Q1+
  //   Q3+
  //   Q2+
endmodule
